# Fritzing sketch FINAL-PROJECT (saved by Fritzing 0.8.7b)
breadboards: 1

parts:
  Part1 = Arduino Mega ADK (Rev3)
  R1 = Resistor [tolerance=±5% resistance=220 package="0603 [SMD]"]
  R2 = Resistor [tolerance=±5% resistance=220 package="0603 [SMD]"]
  C1 = Capacitor Polarized [package=nippon_f80]
  U2 = AD8561 - Ultrafast 7ns Single Supply Comparator [part_number=AD8561]
  R3 = Resistor [tolerance=±5% resistance=220 package="2010 [SMD]"]
  C3 = Capacitor [package=cap-pth-small2]
  L2 = Inductor [package="0603 [SMD]"]
  D2 = Diode [package=diode-1n4001]
  R4 = Resistor [tolerance=±5% resistance=220 package="2010 [SMD]"]

nets:
  N1: Part1.A5, U2.+IN, R3.Pin_1
  N2: Part1.GND, U2.-IN, U2.OUT, C3.1, L2.pin_1
  N3: Part1.D13_PWM, R2.Pin_1, U2.V+, R3.Pin_0, L2.pin_0, D2.A
  N4: Part1.D11_PWM, R1.Pin_0, R4.Pin_0
  N5: R1.Pin_1, R2.Pin_0, C1.-
  N6: U2.V-, C3.2
